# Fritzing sketch circuitdiagram (saved by Fritzing 0.9.4)
breadboards: 1

parts:
  Part1 = Arduino Nano (Rev3.0) (ICSP)
  Part2 = InvenSense MPU6050
  S1 = Momentary Switch [package=ksa_sealed_tac_switch]
  S2 = Momentary Switch [package=ksa_sealed_tac_switch]
  S3 = Momentary Switch [package=ksa_sealed_tac_switch]
  S4 = Momentary Switch [package=ksa_sealed_tac_switch]
  S5 = Momentary Switch [package=ksa_sealed_tac_switch]
  S6 = Momentary Switch [package=ksa_sealed_tac_switch]

nets:
  GND: Part1.GND, Part2.GND, S1.1, S2.1, S3.1, S4.1, S5.1, S6.1
  N1: Part1.D7, S1.3
  N2: Part1.D8, S2.3
  N3: Part1.D9, S3.3
  N4: Part1.D10, S4.3
  N5: Part1.D11/MOSI, S5.3
  N6: Part1.D12/MISO, S6.3
  5V: Part1.5V, Part2.VCC
  N7: Part1.A5, Part2.SCL
  N8: Part1.A4, Part2.SDA
